# Fritzing sketch Automatic active reagent dosing system (saved by Fritzing 0.9.3b)

parts:
  Componente2 = Arduino Uno (Rev3)  # not connected
  Power_plug1 = Power plug  # not connected
  Componente3 = EasyDriver_v44
  M3 = Stepper Motor - Bipolar
  R1 = Resistor [tolerance=±5% resistance=220 package=THT]
  S1 = SWITCH-MOMENTARY-2 [package=tactile_switch_smd]  # not connected

nets:
  N1: Componente3.OUT2A, M3.A
  N2: Componente3.OUT2B, M3.C
  N3: Componente3.OUT1A, M3.B
  N4: Componente3.OUT1B, M3.D
  N5: Componente3.VCC, R1.Pin_1
